# Fritzing sketch LM35_DifOpAmp_DAC (saved by Fritzing 0.9.4)
breadboards: 1

parts:
  U1 = ESP32-38PinWide [part_number=ESP32-38PinWide]
  T1 = LM35 Temperature Sensor [package="TO92 [THT]"]
  U3 = LM358 [package=dip08]
  R2 = Resistor [tolerance=±5% resistance=10k package=THT]
  R3 = Resistor [tolerance=±5% resistance=68k package=THT]
  R5 = Resistor [tolerance=±5% resistance=10k package=THT]
  R6 = Resistor [tolerance=±5% resistance=68k package=THT]

nets:
  N1: U1.GPIO25, R2.Pin_1
  N2: U1.GPIO27, U3.G$1_OUT, R3.Pin_1
  N3: U1.GPIO11, T1.GND, U3.G$1_V-, R6.Pin_0
  N4: U1.VIN, T1.+Vs, U3.G$1_V+
  N5: T1.Vout, R5.Pin_1
  N6: U3.G$1_-IN, R2.Pin_0, R3.Pin_0
  N7: U3.G$1_+IN, R5.Pin_0, R6.Pin_1

custom parts:
  ESP32-38PinWide: Generic 38-Pin ESP32 with wide format (only access to one side of pins on a breadboard) based on Stephen Lilley's HiLetgo ESP-WROOM-32 ESP32 ESP-32S Development Board.
